# Fritzing sketch APS (saved by Fritzing 0.9.3b)

parts:
  U1 = 2-Channel 5v Relay Shield [package=relay-2ch5v10a]
  LED2 = LEDs [package=led10mm]
  Componente2 = Bluetooth HC-05 Macho
  Componente1 = Arduino Mega 2560 (Rev3)

nets:
  VCC: U1.VCC, Componente2.VCC, Componente1.5V
  GND: U1.GND, Componente2.GND, Componente1.GND
  N1: U1.IN1, U1.IN2, Componente1.D8_PWM
  N2: U1.K1-In, LED2.A
  N3: U1.K1-On, LED2.C
  N4: Componente2.TXD, Componente1.D17_PWM/RX2
  N5: Componente2.RXD, Componente1.D16_PWM/TX2

custom parts:
  2-Channel 5v Relay Shield: 2 Channel 5v Relay Shield w. 2x SPD-06VDC-SD-C
  LEDs: LEDs Standard schematic elements and footprints for 5mm, 3mm, 1206, and 0603 sized LEDs. 5mm - Spark Fun Electronics SKU : COM-00529 (and others)

// code stored in the sketch: apsino.ino
#define IN1 8 


void setup() {
  pinMode(IN1, OUTPUT);
  Serial2.begin(9600);
  digitalWrite(IN1, HIGH);
}


void loop() {
  char command;
  while (Serial2.available()) {
    command = Serial2.read();
  }
if (command == 'l'){
    digitalWrite(IN1, LOW);  
}
if (command == 'd'){
    digitalWrite(IN1, HIGH);  
}


}
